# Fritzing sketch Data-Acq (saved by Fritzing 0.9.2b)
circuit board: 7.18895cm x 3.42028cm
breadboards: 1

parts:
  Raspberry_Pi1 = Raspberry Pi B+
  IC1 = MCP3008 8-channel 10-bit ADC [part_number=MCP3008]
  T1 = TMP36 Temperature Sensor [package="TO92 [THT]"]
  T2 = TMP36 Temperature Sensor [package="TO92 [THT]"]
  T3 = TMP36 Temperature Sensor [package="TO92 [THT]"]
  T4 = TMP36 Temperature Sensor [package="TO92 [THT]"]
  U1 = LCD-16X2 [package=lcd-16x2]
  R1 = TRIMPOT [package=3362u-2]
  S1 = Round Pushbutton
  S2 = Round Pushbutton
  S3 = Round Pushbutton
  S4 = Round Pushbutton
  S5 = JOYSTICK_MINI [package=joystick_mini]

nets (from the breadboard view):
  3V3: Raspberry_Pi1.3v3, Raspberry_Pi1.3V3, IC1.no_name_yet#15, IC1.no_name_yet#16, T1.+Vs
  N1: Raspberry_Pi1.GPIO4, S3.leg0
  GND: Raspberry_Pi1.GND, IC1.no_name_yet#9, IC1.no_name_yet#14, T1.GND, U1.VSS, S1.leg1
  N2: Raspberry_Pi1.GPIO17, S4.leg0
  N3: Raspberry_Pi1.GPIO27, S1.leg0
  N4: Raspberry_Pi1.GPIO22, S2.leg0
  N5: Raspberry_Pi1.GPIO5, S5.LEFT
  N6: Raspberry_Pi1.GPIO6, S5.RIGHT
  N7: Raspberry_Pi1.GPIO13, S5.UP
  N8: Raspberry_Pi1.GPIO19, U1.RS
  N9: Raspberry_Pi1.GPIO26, U1.E
  N10: Raspberry_Pi1.GPIO21, U1.DB7
  N11: Raspberry_Pi1.GPIO20, U1.DB4
  N12: Raspberry_Pi1.GPIO16, U1.DB5
  N13: Raspberry_Pi1.GPIO12, U1.DB6
  N14: Raspberry_Pi1.GPIO7, S5.DOWN
  N15: Raspberry_Pi1.GPIO8, S5.CENT
  N16: Raspberry_Pi1.GPIO25, IC1.no_name_yet#10
  N17: Raspberry_Pi1.GPIO24, IC1.no_name_yet#11
  N18: Raspberry_Pi1.GPIO23, IC1.no_name_yet#12
  N19: Raspberry_Pi1.GPIO18, IC1.no_name_yet#13
  N20: Raspberry_Pi1.5V, R1.CCW
  N21: IC1.no_name_yet#1, T1.Vout
  N22: IC1.no_name_yet#2, T2.Vout
  N23: IC1.no_name_yet#3, T3.Vout
  N24: IC1.no_name_yet#4, T4.Vout
  N25: U1.VO, R1.WIPER
